# Fritzing sketch 回路図 (saved by Fritzing 0.9.3b)
breadboards: 1

parts:
  TWE-Lite(DIP)1 = TWE-Lite DIP [package=DIP]
  Q1 = NPN-Transistor [part_number=2SC1815 package="TO92 [THT]"]
  R1 = Resistor [tolerance=±5% resistance=10k package=THT]
  パーツ1 = Adafruit ADS1115 16Bit I2C ADC [part_number="SWITCH SCIENCE ADS1115"]
  R2 = Resistor [tolerance=±5% resistance=100 part_number=(Pt100温度センサ) package=THT]
  R3 = Resistor [tolerance=±5% resistance=100 part_number=(基準抵抗) package=THT]
  VCC1 = Battery

nets:
  GND: TWE-Lite(DIP)1.GND, Q1.E, パーツ1.ADDR, パーツ1.GND, VCC1.-
  N1: TWE-Lite(DIP)1.I2C_SCL, パーツ1.SCL
  N2: TWE-Lite(DIP)1.DO_4, R1.Pin_0
  N3: TWE-Lite(DIP)1.I2C_SDA, パーツ1.SDA
  VCC: TWE-Lite(DIP)1.VCC, パーツ1.AIN0, パーツ1.VDD, R2.Pin_0, VCC1.+
  N4: Q1.B, R1.Pin_1
  N5: Q1.C, パーツ1.AIN3, R3.Pin_1
  N6: パーツ1.AIN1, R2.Pin_1, R3.Pin_0

custom parts:
  TWE-Lite DIP: TWE-Lite for DIP. 28 pins.
  Adafruit ADS1115 16Bit I2C ADC: For microcontrollers without an analog-to-digital converter or when you want a higher-precision ADC, the ADS1115 provides 16-bit precision at 860 samples/second over I2C. The chip can be configured as 4 single-ended input channels, or two differential channels. As a nice bonus, it even includes a programmable gain amplifier, up to x16, to help boost up smaller single/differential signals to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
